# Fritzing sketch Wireless Haptic Circuit Layout (saved by Fritzing 0.9.3b)

parts:
  WeMos_D1_Mini1 = WeMos D1 Mini
  Q1 = NPN-Transistor [package="TO92 [THT]"]
  Q2 = Basic FET P-Channel [package="TO220 [THT]"]
  R1 = Resistor [tolerance=±5% resistance=220 package=THT]
  VCC1 = Battery block 9V
  Lilypad_Vibe1 = Lilypad Vibe Motor

nets:
  N1: WeMos_D1_Mini1.5V, Q2.source
  N2: WeMos_D1_Mini1.D3, R1.Pin_1
  N3: WeMos_D1_Mini1.G, VCC1.-
  N4: Q1.B, R1.Pin_0
  N5: Q1.C, Lilypad_Vibe1.GND
  N6: Q2.gate, VCC1.+

custom parts:
  WeMos D1 Mini: The D1 mini is a mini wifi board based on ESP-8266EX.
